# Fritzing sketch Esquematico (saved by Fritzing 0.9.3b)
breadboards: 1

parts:
  Componente1 = Arduino Uno (Rev3)
  Fuente_de_alimentación = BC9VPC [package=bc9vpc]
  Seguidor_De_Voltaje = OP37 - Low Noise, Precision, High Speed Op Amp [part_number=OP37]
  Thinxtra = Arduino Micro (Rev3)
  Resistencia_Pull_Down = Resistor [tolerance=±5% resistance=10k package=THT]
  Sensor_Velostat = Textile Analog Pressure Sensor [part_number=PW073]
  Divisor_de_Tensión = Resistor [tolerance=±5% resistance=1k package=THT]
  Divisor_de_Tensión_2 = Resistor [tolerance=±5% resistance=1k package=THT]

nets:
  5V: Componente1.A0, Componente1.5V, Thinxtra.VIN, Resistencia_Pull_Down.Pin_1, Sensor_Velostat.pin_1
  N1: Componente1.A1, Seguidor_De_Voltaje.-IN, Seguidor_De_Voltaje.OUT
  N2: Componente1.D0/RX, Thinxtra.D0/RX
  N3: Componente1.D1/TX, Thinxtra.D1/TX
  GND: Componente1.GND, Fuente_de_alimentación.V-, Seguidor_De_Voltaje.-V, Thinxtra.GND, Resistencia_Pull_Down.Pin_0, Sensor_Velostat.pin_0, Divisor_de_Tensión_2.Pin_0
  12V: Componente1.VIN, Fuente_de_alimentación.V+, Seguidor_De_Voltaje.V+, Divisor_de_Tensión.Pin_0
  N4: Seguidor_De_Voltaje.+IN, Divisor_de_Tensión.Pin_1, Divisor_de_Tensión_2.Pin_1
