# Fritzing sketch Esquematico (saved by Fritzing 0.9.3b)
breadboards: 1

parts:
  Componente1 = Arduino Uno (Rev3)
  Sensor_Velostat = Basic Force Sensing Resistor (FSR) [package=THT]
  Fuente_de_alimentación = BC9VPC [package=bc9vpc]

nets:
  N1: Componente1.A0, Componente1.5V, Sensor_Velostat.pin_1
  N2: Componente1.GND, Sensor_Velostat.pin_0, Fuente_de_alimentación.V-
  12V: Componente1.VIN, Fuente_de_alimentación.V+
